// Logisim project Processor.circ as structural Verilog: 19 circuits, main circuit Pipelined Processor
module Control_Unit (
  input  I_bit,
  input  [4:0] opcode,
  output isSt,
  output isLd,
  output isBeq,
  output isBgt,
  output isRet,
  output isImmediate,
  output isWb,
  output isUbranch,
  output isCall,
  output [12:0] ALUsignals
);

  wire and_6_out, and_7_out, and_8_out, and_9_out, and_10_out, and_12_out, and_13_out, nand_1_out;

  nand nand_1 (nand_1_out, opcode[0], opcode[1]);
  and and_1 (isSt, opcode[0], opcode[1], opcode[2], opcode[3], ~opcode[4]);  // AND_Gate
  and and_2 (isLd, ~opcode[0], opcode[1], opcode[2], opcode[3], ~opcode[4]);  // AND_Gate
  and and_3 (isBeq, ~opcode[0], ~opcode[1], ~opcode[2], ~opcode[3], opcode[4]);  // AND_Gate
  and and_4 (isBgt, opcode[0], ~opcode[1], ~opcode[2], ~opcode[3], opcode[4]);  // AND_Gate
  and and_5 (isRet, ~opcode[0], ~opcode[1], opcode[2], ~opcode[3], opcode[4]);  // AND_Gate
  and and_6 (and_6_out, opcode[0], ~opcode[1], opcode[2], ~opcode[4]);  // AND_Gate
  and and_7 (and_7_out, opcode[0], opcode[2], opcode[3], ~opcode[4]);  // AND_Gate
  and and_8 (and_8_out, opcode[4], nand_1_out);
  and and_9 (and_9_out, opcode[1], ~opcode[2], ~opcode[3], opcode[4]);  // AND_Gate
  and and_10 (and_10_out, ~opcode[0], ~opcode[1], opcode[2], ~opcode[3], opcode[4]);  // AND_Gate
  and and_11 (isCall, opcode[0], opcode[1], ~opcode[2], ~opcode[3], opcode[4]);  // AND_Gate
  and and_12 (and_12_out, ~opcode[0], ~opcode[1], ~opcode[2], ~opcode[3], ~opcode[4]);  // AND_Gate
  and and_13 (and_13_out, opcode[1], opcode[2], opcode[3], ~opcode[4]);  // AND_Gate
  and isSub (ALUsignals[2], opcode[0], ~opcode[1], ~opcode[2], ~opcode[3], ~opcode[4]);  // AND_Gate
  and isCmp (ALUsignals[0], opcode[0], ~opcode[1], opcode[2], ~opcode[3], ~opcode[4]);  // AND_Gate
  and isMul (ALUsignals[3], ~opcode[0], opcode[1], ~opcode[2], ~opcode[3], ~opcode[4]);  // AND_Gate
  and isDiv (ALUsignals[4], opcode[0], opcode[1], ~opcode[2], ~opcode[3], ~opcode[4]);  // AND_Gate
  and isMod (ALUsignals[5], ~opcode[0], ~opcode[1], opcode[2], ~opcode[3], ~opcode[4]);  // AND_Gate
  and isLsl (ALUsignals[7], ~opcode[0], opcode[1], ~opcode[2], opcode[3], ~opcode[4]);  // AND_Gate
  and isLsr (ALUsignals[8], opcode[0], opcode[1], ~opcode[2], opcode[3], ~opcode[4]);  // AND_Gate
  and isAsr (ALUsignals[9], ~opcode[0], ~opcode[1], opcode[2], opcode[3], ~opcode[4]);  // AND_Gate
  and isOr (ALUsignals[12], opcode[0], opcode[1], opcode[2], ~opcode[3], ~opcode[4]);  // AND_Gate
  and isAnd (ALUsignals[11], ~opcode[0], opcode[1], opcode[2], ~opcode[3], ~opcode[4]);  // AND_Gate
  and isNot (ALUsignals[10], ~opcode[0], ~opcode[1], ~opcode[2], opcode[3], ~opcode[4]);  // AND_Gate
  and isMov (ALUsignals[6], opcode[0], ~opcode[1], ~opcode[2], opcode[3], ~opcode[4]);  // AND_Gate
  or or_1 (isUbranch, and_9_out, and_10_out);
  or isAdd (ALUsignals[1], and_12_out, and_13_out);
  nor nor_1 (isWb, and_6_out, and_7_out, and_8_out);

  assign isImmediate = I_bit;

  // Notes on the sheet:
  //   op1
  //   op2
  //   op3
  //   op4
  //   op5
endmodule

module Processor (
  input  Reset,
  input  [3:0] Display_Address
);

  wire alu_1_is, alu_1_is_2, branch_unit_1_isbranchtaken, Clock, control_unit_1_isbeq, control_unit_1_isbgt,
       control_unit_1_isimmediate, control_unit_1_isret, control_unit_1_isst, control_unit_1_isubranch,
       control_unit_1_iswb, flags_1_flags_e, flags_1_flags_gt;
  wire [1:0] control_unit_1_isld;
  wire [3:0] multiplexer_5_out, multiplexer_6_out, multiplexer_7_out, register_file_1_displayd,
       register_file_1_displayd_2, register_file_1_displayd_4, register_file_1_displayd_5,
       register_file_1_displayd_6, register_file_1_displayd_7, register_file_1_displayd_8, rom_1_data_2;
  wire [11:8] register_file_1_displayd_3;
  wire [12:0] control_unit_1_alusignals;
  wire [26:0] rom_1_data;
  wire [31:0] adder_1_out, adder_2_out, adder_3_out, alu_1_aluresult, bit_extender_1_out,
       calculate_immediate_1_immx, memory_unit_1_ldresult, multiplexer_1_out, multiplexer_2_out,
       multiplexer_3_out, multiplexer_4_out, PC_q, register_file_1_readd1, register_file_1_readd2,
       shifter_1_out;
  wire [31:27] rom_1_data_3;

  Register #(.width(32), .trigger("falling")) PC (
    .D(multiplexer_1_out), .Q(PC_q), .clk(Clock), .clr(Reset));  // open: en
  Multiplexer #(.width(32), .enable("false")) multiplexer_1 (
    .in0(adder_1_out), .in1(multiplexer_2_out), .out(multiplexer_1_out), .sel(branch_unit_1_isbranchtaken));
  assign bit_extender_1_out = {{5{rom_1_data[26]}}, {rom_1_data[26], rom_1_data_2, rom_1_data[21:0]}};  // Bit_Extender bit_extender_1
  ALU alu_1 (
    .A(register_file_1_readd1), .B(multiplexer_4_out), .ALUsignals(control_unit_1_alusignals),
    .aluResult(alu_1_aluresult), .is_2(alu_1_is_2), .is(alu_1_is));
  Adder #(.width(32)) adder_1 (.a(32'h4), .b(PC_q), .out(adder_1_out));  // open: cin, cout
  Shifter #(.width(32)) shifter_1 (.in(bit_extender_1_out), .\dist (5'b00010), .out(shifter_1_out));
  Adder #(.width(32)) adder_2 (.a(PC_q), .b(32'h4), .out(adder_2_out));  // open: cin, cout
  Calculate_Immediate calculate_immediate_1 (.imm(rom_1_data[17:0]), .immx(calculate_immediate_1_immx));
  Adder #(.width(32)) adder_3 (.a(shifter_1_out), .b(PC_q), .out(adder_3_out));  // open: cin, cout
  Multiplexer #(.width(32), .enable("false")) multiplexer_2 (
    .in0(adder_3_out), .in1(register_file_1_readd1), .out(multiplexer_2_out), .sel(control_unit_1_isret));
  Multiplexer #(.select(2), .width(32), .enable("false")) multiplexer_3 (
    .in0(alu_1_aluresult), .in1(memory_unit_1_ldresult), .in2(adder_2_out), .out(multiplexer_3_out),
    .sel(control_unit_1_isld));  // open: in3
  Clock u_Clock (.out(Clock));
  ROM #(.addrWidth(24), .dataWidth(32)) rom_1 (
    .addr(PC_q[25:2]), .data({rom_1_data_3, rom_1_data[26], rom_1_data_2, rom_1_data[21:0]}));  // open: sel
  Multiplexer #(.width(32), .enable("false")) multiplexer_4 (
    .in0(register_file_1_readd2), .in1(calculate_immediate_1_immx), .out(multiplexer_4_out),
    .sel(control_unit_1_isimmediate));
  Flags flags_1 (
    .isCmp(control_unit_1_alusignals[0]), .is(alu_1_is), .is_2(alu_1_is_2), .flags_GT(flags_1_flags_gt),
    .flags_E(flags_1_flags_e));
  Memory_Unit memory_unit_1 (
    .MAR(alu_1_aluresult), .ldResult(memory_unit_1_ldresult), .MDR(register_file_1_readd2),
    .isSt(control_unit_1_isst), .isLd(control_unit_1_isld[0]), .Clock(Clock), .Reset(Reset));
  Hex_Digit_Display hex_digit_display_1 (.value(register_file_1_displayd_8));  // open: dp
  Multiplexer #(.width(4), .enable("false")) multiplexer_5 (
    .in0(rom_1_data[17:14]), .in1(rom_1_data_2), .out(multiplexer_5_out), .sel(control_unit_1_isst));
  Hex_Digit_Display hex_digit_display_2 (.value(register_file_1_displayd_7));  // open: dp
  Multiplexer #(.width(4), .enable("false")) multiplexer_6 (
    .in0(rom_1_data[21:18]), .in1(4'b1111), .out(multiplexer_6_out), .sel(control_unit_1_isret));
  Register_File register_file_1 (
    .ReadA1(multiplexer_6_out), .ReadA2(multiplexer_5_out), .WriteE(control_unit_1_iswb),
    .WriteD(multiplexer_3_out), .ReadD1(register_file_1_readd1), .ReadD2(register_file_1_readd2),
    .Clock(Clock), .Reset(Reset),
    .DisplayD({register_file_1_displayd_8, register_file_1_displayd_7, register_file_1_displayd_6, register_file_1_displayd_5, register_file_1_displayd_4, register_file_1_displayd_3, register_file_1_displayd_2, register_file_1_displayd}),
    .DisplayA(Display_Address), .WriteA(multiplexer_7_out));
  Hex_Digit_Display hex_digit_display_3 (.value(register_file_1_displayd_6));  // open: dp
  Branch_Unit branch_unit_1 (
    .isBeq(control_unit_1_isbeq), .isUBranch(control_unit_1_isubranch), .flags_E(flags_1_flags_e),
    .isBgt(control_unit_1_isbgt), .flags_GT(flags_1_flags_gt), .isBranchTaken(branch_unit_1_isbranchtaken));
  Hex_Digit_Display hex_digit_display_4 (.value(register_file_1_displayd_5));  // open: dp
  Hex_Digit_Display hex_digit_display_5 (.value(register_file_1_displayd_4));  // open: dp
  Control_Unit control_unit_1 (
    .isSt(control_unit_1_isst), .isLd(control_unit_1_isld[0]), .isBeq(control_unit_1_isbeq),
    .isBgt(control_unit_1_isbgt), .isRet(control_unit_1_isret), .I_bit(rom_1_data[26]),
    .isImmediate(control_unit_1_isimmediate), .opcode(rom_1_data_3), .isWb(control_unit_1_iswb),
    .isUbranch(control_unit_1_isubranch), .isCall(control_unit_1_isld[1]),
    .ALUsignals(control_unit_1_alusignals));
  Hex_Digit_Display hex_digit_display_6 (.value(register_file_1_displayd_3));  // open: dp
  Hex_Digit_Display hex_digit_display_7 (.value(register_file_1_displayd_2));  // open: dp
  Multiplexer #(.width(4), .enable("false")) multiplexer_7 (
    .in0(rom_1_data_2), .in1(4'b1111), .out(multiplexer_7_out), .sel(control_unit_1_isld[1]));
  Hex_Digit_Display hex_digit_display_8 (.value(register_file_1_displayd));  // open: dp

  // Notes on the sheet:
  //   SINGLE CYCLE PROCESSOR
  //   isBranchTaken
  //   ALUsignals
  //   pc
  //   pc+4
  //   branchTarget
  //   offset
  //   pc
  //   B
  //   ALU
  //   aluResult
  //   MAR
  //   calc immx
  //   imm
  //   branchTarget
  //   isBranchTaken
  //   A
  //   is>
  //   is=
  //   MDR
  //   Memory
  //   Unit
  //   ldResult
  //   data
  //   Instruction Memory
  //   contents of rom_1 (hex, n*v repeats v):
  //   4c800002 4cc00003 4d400005 4d800006 4e400009 4e80000a 98000004 48c000 9058000 90000000 2268000
  //   a0000000
  //   immx
  //   isRet
  //   Flags
  //   isCmp
  //   isLd
  //   isSt
  //   isLd
  //   isCall
  //   instruction
  //   rs2
  //   rd
  //   isSt
  //   op2
  //   isImmediate
  //   flags(GT)
  //   flags(E)
  //   rs1
  //   E
  //   Register
  //   A
  //   File
  //   D
  //   op1
  //   Branch
  //   Unit
  //   isRet
  //   isWb
  //   address
  //   data
  //   isBeq
  //   isBgt
  //   isUBranch
  //   Display Register
  //   opcode
  //   CONTROL
  //   I bit
  //   UNIT
  //   isCall
  //   rd
endmodule

module Register_File (
  input  Clock,
  input  Reset,
  input  [31:0] WriteD,
  input  [3:0] ReadA1,
  input  WriteE,
  input  [3:0] WriteA,
  input  [3:0] ReadA2,
  input  [3:0] DisplayA,
  output [31:0] ReadD1,
  output [31:0] ReadD2,
  output [31:0] DisplayD
);

  wire demultiplexer_1_out0, demultiplexer_1_out1, demultiplexer_1_out2, demultiplexer_1_out3,
       demultiplexer_1_out4, demultiplexer_1_out5, demultiplexer_1_out6, demultiplexer_1_out7,
       demultiplexer_1_out8, demultiplexer_1_out9, demultiplexer_1_out10, demultiplexer_1_out11,
       demultiplexer_1_out12, demultiplexer_1_out13, demultiplexer_1_out14, demultiplexer_1_out15,
       multiplexer_2_out, or_1_out, or_2_out;
  wire [31:0] multiplexer_1_out, r0_q, r1_q, r2_q, r3_q, r4_q, r5_q, r6_q, r7_q, r8_q, r9_q, r10_q, r11_q,
       r12_q, r13_q, r14_q, r15_q;

  Demultiplexer #(.select(4), .disabled(0), .enable("false")) demultiplexer_1 (
    .out0(demultiplexer_1_out0), .out1(demultiplexer_1_out1), .out2(demultiplexer_1_out2),
    .out3(demultiplexer_1_out3), .out4(demultiplexer_1_out4), .out5(demultiplexer_1_out5),
    .out6(demultiplexer_1_out6), .out7(demultiplexer_1_out7), .out8(demultiplexer_1_out8),
    .out9(demultiplexer_1_out9), .out10(demultiplexer_1_out10), .out11(demultiplexer_1_out11),
    .out12(demultiplexer_1_out12), .out13(demultiplexer_1_out13), .out14(demultiplexer_1_out14),
    .out15(demultiplexer_1_out15), .in(WriteE), .sel(WriteA));
  Multiplexer #(.width(32), .enable("false")) multiplexer_1 (
    .in0(WriteD), .in1(32'h3fffffc), .out(multiplexer_1_out), .sel(Reset));
  or or_1 (or_1_out, demultiplexer_1_out14, Reset);
  Multiplexer #(.enable("false")) multiplexer_2 (.in0(or_2_out), .out(multiplexer_2_out), .sel(1'b0));  // open: in1
  or or_2 (or_2_out, Clock, Reset);
  Register #(.width(32)) r0 (.D(WriteD), .en(demultiplexer_1_out0), .Q(r0_q), .clk(Clock), .clr(Reset));
  Register #(.width(32)) r1 (.D(WriteD), .en(demultiplexer_1_out1), .Q(r1_q), .clk(Clock), .clr(Reset));
  Register #(.width(32)) r2 (.D(WriteD), .en(demultiplexer_1_out2), .Q(r2_q), .clk(Clock), .clr(Reset));
  Register #(.width(32)) r3 (.D(WriteD), .en(demultiplexer_1_out3), .Q(r3_q), .clk(Clock), .clr(Reset));
  Register #(.width(32)) r4 (.D(WriteD), .en(demultiplexer_1_out4), .Q(r4_q), .clk(Clock), .clr(Reset));
  Register #(.width(32)) r5 (.D(WriteD), .en(demultiplexer_1_out5), .Q(r5_q), .clk(Clock), .clr(Reset));
  Register #(.width(32)) r6 (.D(WriteD), .en(demultiplexer_1_out6), .Q(r6_q), .clk(Clock), .clr(Reset));
  Register #(.width(32)) r7 (.D(WriteD), .en(demultiplexer_1_out7), .Q(r7_q), .clk(Clock), .clr(Reset));
  Register #(.width(32)) r8 (.D(WriteD), .en(demultiplexer_1_out8), .Q(r8_q), .clk(Clock), .clr(Reset));
  Register #(.width(32)) r9 (.D(WriteD), .en(demultiplexer_1_out9), .Q(r9_q), .clk(Clock), .clr(Reset));
  Register #(.width(32)) r10 (.D(WriteD), .en(demultiplexer_1_out10), .Q(r10_q), .clk(Clock), .clr(Reset));
  Register #(.width(32)) r11 (.D(WriteD), .en(demultiplexer_1_out11), .Q(r11_q), .clk(Clock), .clr(Reset));
  Register #(.width(32)) r12 (.D(WriteD), .en(demultiplexer_1_out12), .Q(r12_q), .clk(Clock), .clr(Reset));
  Register #(.width(32)) r13 (.D(WriteD), .en(demultiplexer_1_out13), .Q(r13_q), .clk(Clock), .clr(Reset));
  Register #(.width(32)) r14 (.D(multiplexer_1_out), .en(or_1_out), .Q(r14_q), .clk(multiplexer_2_out));  // open: clr
  Register #(.width(32)) r15 (.D(WriteD), .en(demultiplexer_1_out15), .Q(r15_q), .clk(Clock), .clr(Reset));
  Multiplexer #(.select(4), .width(32), .disabled(0), .enable("false")) multiplexer_3 (
    .in0(r0_q), .in1(r1_q), .in2(r2_q), .in3(r3_q), .in4(r4_q), .in5(r5_q), .in6(r6_q), .in7(r7_q),
    .in8(r8_q), .in9(r9_q), .in10(r10_q), .in11(r11_q), .in12(r12_q), .in13(r13_q), .in14(r14_q),
    .in15(r15_q), .out(ReadD1), .sel(ReadA1));
  Multiplexer #(.select(4), .width(32), .disabled(0), .enable("false")) multiplexer_4 (
    .in0(r0_q), .in1(r1_q), .in2(r2_q), .in3(r3_q), .in4(r4_q), .in5(r5_q), .in6(r6_q), .in7(r7_q),
    .in8(r8_q), .in9(r9_q), .in10(r10_q), .in11(r11_q), .in12(r12_q), .in13(r13_q), .in14(r14_q),
    .in15(r15_q), .out(ReadD2), .sel(ReadA2));
  Multiplexer #(.select(4), .width(32), .disabled(0), .enable("false")) multiplexer_5 (
    .in0(r0_q), .in1(r1_q), .in2(r2_q), .in3(r3_q), .in4(r4_q), .in5(r5_q), .in6(r6_q), .in7(r7_q),
    .in8(r8_q), .in9(r9_q), .in10(r10_q), .in11(r11_q), .in12(r12_q), .in13(r13_q), .in14(r14_q),
    .in15(r15_q), .out(DisplayD), .sel(DisplayA));
endmodule

module ALU (
  input  [31:0] A,
  input  [31:0] B,
  input  [12:0] ALUsignals,
  output [31:0] aluResult,
  output is,
  output is_2
);

  wire [31:0] adder_1_out, and_1_out, divider_1_out, divider_1_rem, multiplier_1_out, not_1_out, or_1_out,
       shifter_1_out, shifter_2_out, shifter_3_out, subtractor_1_out;

  Adder #(.width(32)) adder_1 (.a(A), .b(B), .out(adder_1_out));  // open: cin, cout
  Subtractor #(.width(32)) subtractor_1 (.a(A), .b(B), .out(subtractor_1_out));  // open: bin, bout
  Multiplier #(.width(32)) multiplier_1 (.a(A), .b(B), .out(multiplier_1_out));  // open: cin, cout
  Divider #(.width(32)) divider_1 (.a(A), .b(B), .out(divider_1_out), .rem(divider_1_rem));  // open: upper
  Comparator #(.width(32)) comparator_1 (.a(A), .b(B), .gt(is), .eq(is_2));  // open: lt
  Shifter #(.width(32)) shifter_1 (.in(A), .\dist (B[4:0]), .out(shifter_1_out));
  Shifter #(.width(32), .shift("lr")) shifter_2 (.in(A), .\dist (B[4:0]), .out(shifter_2_out));
  Shifter #(.width(32), .shift("ar")) shifter_3 (.in(A), .\dist (B[4:0]), .out(shifter_3_out));
  assign not_1_out = ~B;  // NOT_Gate not_1, 32 bits wide
  assign and_1_out = A & B;  // AND_Gate and_1, 32 bits wide
  assign or_1_out = A | B;  // OR_Gate or_1, 32 bits wide
  assign aluResult = ALUsignals[1] ? adder_1_out : 32'bz;  // Controlled_Buffer controlled_buffer_1
  assign aluResult = ALUsignals[2] ? subtractor_1_out : 32'bz;  // Controlled_Buffer controlled_buffer_2
  assign aluResult = ALUsignals[3] ? multiplier_1_out : 32'bz;  // Controlled_Buffer controlled_buffer_3
  assign aluResult = ALUsignals[4] ? divider_1_out : 32'bz;  // Controlled_Buffer controlled_buffer_4
  assign aluResult = ALUsignals[5] ? divider_1_rem : 32'bz;  // Controlled_Buffer controlled_buffer_5
  assign aluResult = ALUsignals[6] ? B : 32'bz;  // Controlled_Buffer controlled_buffer_6
  assign aluResult = ALUsignals[7] ? shifter_1_out : 32'bz;  // Controlled_Buffer controlled_buffer_7
  assign aluResult = ALUsignals[8] ? shifter_2_out : 32'bz;  // Controlled_Buffer controlled_buffer_8
  assign aluResult = ALUsignals[9] ? shifter_3_out : 32'bz;  // Controlled_Buffer controlled_buffer_9
  assign aluResult = ALUsignals[10] ? not_1_out : 32'bz;  // Controlled_Buffer controlled_buffer_10
  assign aluResult = ALUsignals[11] ? and_1_out : 32'bz;  // Controlled_Buffer controlled_buffer_11
  assign aluResult = ALUsignals[12] ? or_1_out : 32'bz;  // Controlled_Buffer controlled_buffer_12

  // Notes on the sheet:
  //   add
  //   sub
  //   mul
  //   div
  //   cmp
  //   lsr
  //   mod
  //   lsl
  //   asr
endmodule

module Flags (
  input  isCmp,
  input  is,
  input  is_2,
  output flags_GT,
  output flags_E
);

  D_Flip_Flop #(.trigger("high")) d_ff_1 (.clk(isCmp), .D(is), .Q(flags_GT));  // open: Qn, preset, en, reset
  D_Flip_Flop #(.trigger("high")) d_ff_2 (.clk(isCmp), .D(is_2), .Q(flags_E));  // open: Qn, preset, en, reset
endmodule

module Branch_Unit (
  input  isUBranch,
  input  isBeq,
  input  flags_E,
  input  isBgt,
  input  flags_GT,
  output isBranchTaken
);

  wire and_1_out, and_2_out;

  and and_1 (and_1_out, isBeq, flags_E);
  and and_2 (and_2_out, isBgt, flags_GT);
  or or_1 (isBranchTaken, isUBranch, and_1_out, and_2_out);
endmodule

module Memory_Unit (
  input  [31:0] MAR,
  input  isLd,
  input  [31:0] MDR,
  input  isSt,
  input  Clock,
  input  Reset,
  output [31:0] ldResult
);

  RAM #(.addrWidth(24), .dataWidth(32), .bus("separate")) ram_1 (
    .addr(MAR[25:2]), .din(MDR), .data(ldResult), .str(isSt), .clk(Clock), .ld(isLd), .clr(Reset));  // open: sel
endmodule

module control (
  input  isRet,
  input  isWb,
  input  [12:0] ALUsignals,
  input  isLd,
  input  isSt,
  input  isCall,
  input  isBeq,
  input  isBgt,
  input  isUBranch,
  input  Bubble,
  input  in_11,
  input  in_12,
  output isRet_2,
  output isWb_2,
  output [12:0] ALUsignals_2,
  output isLd_2,
  output isSt_2,
  output isCall_2,
  output isBeq_2,
  output isBgt_2,
  output isUBranch_2
);

  wire [7:0] multiplexer_2_out;
  wire [12:0] multiplexer_1_out;

  Register #(.width(1), .trigger("falling")) register_1 (
    .D(multiplexer_2_out[7]), .Q(isRet_2), .clk(in_11), .clr(in_12));  // open: en
  Multiplexer #(.width(13), .enable("false")) multiplexer_1 (
    .in0(ALUsignals), .in1({13{1'b0}}), .out(multiplexer_1_out), .sel(Bubble));
  Register #(.width(1), .trigger("falling")) register_2 (
    .D(multiplexer_2_out[6]), .Q(isWb_2), .clk(in_11), .clr(in_12));  // open: en
  Register #(.width(13), .trigger("falling")) register_3 (
    .D(multiplexer_1_out), .Q(ALUsignals_2), .clk(in_11), .clr(in_12));  // open: en
  Register #(.width(1), .trigger("falling")) register_4 (
    .D(multiplexer_2_out[5]), .Q(isLd_2), .clk(in_11), .clr(in_12));  // open: en
  Register #(.width(1), .trigger("falling")) register_5 (
    .D(multiplexer_2_out[4]), .Q(isSt_2), .clk(in_11), .clr(in_12));  // open: en
  Multiplexer #(.width(8), .enable("false")) multiplexer_2 (
    .in0({isRet, isWb, isLd, isSt, isCall, isBeq, isBgt, isUBranch}), .in1({8{1'b0}}),
    .out(multiplexer_2_out), .sel(Bubble));
  Register #(.width(1), .trigger("falling")) register_6 (
    .D(multiplexer_2_out[3]), .Q(isCall_2), .clk(in_11), .clr(in_12));  // open: en
  Register #(.width(1), .trigger("falling")) register_7 (
    .D(multiplexer_2_out[2]), .Q(isBeq_2), .clk(in_11), .clr(in_12));  // open: en
  Register #(.width(1), .trigger("falling")) register_8 (
    .D(multiplexer_2_out[1]), .Q(isBgt_2), .clk(in_11), .clr(in_12));  // open: en
  Register #(.width(1), .trigger("falling")) register_9 (
    .D(multiplexer_2_out[0]), .Q(isUBranch_2), .clk(in_11), .clr(in_12));  // open: en

  // Notes on the sheet:
  //   if conflict, insert bubble -> insert nop
endmodule

module Calculate_Immediate (
  input  [17:0] imm,
  output [31:0] immx
);

  wire [31:0] bit_extender_1_out, bit_extender_2_out, shifter_1_out;

  assign bit_extender_1_out = {{16{1'b0}}, imm[15:0]};  // Bit_Extender bit_extender_1
  assign bit_extender_2_out = {{16{imm[15]}}, imm[15:0]};  // Bit_Extender bit_extender_2
  Shifter #(.width(32)) shifter_1 (.in(bit_extender_1_out), .\dist (5'b10000), .out(shifter_1_out));
  Multiplexer #(.select(2), .width(32), .enable("false")) multiplexer_1 (
    .in0(bit_extender_2_out), .in1(bit_extender_1_out), .in2(shifter_1_out), .out(immx), .sel(imm[17:16]));  // open: in3

  // Notes on the sheet:
  //   modifier bits
  //   high
  //   default
  //   unsigned
endmodule

// B
module Pipelined_Processor (
  input  Reset,
  input  [3:0] Display_Address
);

  wire alu_1_is, alu_1_is_2, Bubble, Clock, control_1_isbeq_2, control_1_isbgt_2, control_1_iscall_2,
       control_1_isld_2, control_1_isret_2, control_1_isst_2, control_1_isubranch_2, control_1_iswb_2,
       control_ex_ma_1_iscall_2, control_ex_ma_1_isld_2, control_ex_ma_1_isst_2, control_ex_ma_1_iswb_2,
       control_unit_1_isbeq, control_unit_1_isbgt, control_unit_1_iscall, control_unit_1_isimmediate,
       control_unit_1_isld, control_unit_1_isret, control_unit_1_isst, control_unit_1_isubranch,
       control_unit_1_iswb, data_lock_unit_1_out_3, flags_1_flags_e, flags_1_flags_gt,
       forwarding_unit_1_for_op1_op2_mux, forwarding_unit_1_for_op2_mux, forwarding_unit_1_for_op2_mux_2,
       forwarding_unit_1_out_7, isBranchTaken, isWb, Stall;
  wire [1:0] control_ma_rw_1_isld_2, forwarding_unit_1_for_op1_a__mux, forwarding_unit_1_for_op2_b__mux;
  wire [3:0] address, multiplexer_7_out, multiplexer_8_out, register_file_1_displayd,
       register_file_1_displayd_2, register_file_1_displayd_4, register_file_1_displayd_5,
       register_file_1_displayd_6, register_file_1_displayd_7;
  wire [12:0] control_1_alusignals_2, control_unit_1_alusignals;
  wire [31:0] adder_1_out, adder_2_out, adder_3_out, alu_1_aluresult, aluResult, bit_extender_1_out,
       branchTarget, calculate_immediate_1_immx, data, EX_MA_instr, IF_OF_instr, MA_RW_instr,
       memory_unit_1_ldresult, multiplexer_1_out, multiplexer_3_out, multiplexer_4_out, multiplexer_5_out,
       multiplexer_6_out, multiplexer_9_out, multiplexer_10_out, multiplexer_12_out, multiplexer_13_out,
       multiplexer_15_out, OF_EX_instr, PC_q, register_1_q, register_2_q, register_3_q, register_4_q,
       register_5_q, register_6_q, register_8_q, register_9_q, register_10_q, register_11_q, register_13_q,
       register_file_1_readd1, register_file_1_readd2, rom_1_data, shifter_1_out;
  wire [31:8] register_file_1_displayd_3;

  Data_Lock_Unit data_lock_unit_1 (.out_3(data_lock_unit_1_out_3), .B(OF_EX_instr), .A(IF_OF_instr));
  Forwarding_Unit forwarding_unit_1 (
    .MA_RW(MA_RW_instr), .EX_MA(EX_MA_instr), .IF_OF(IF_OF_instr), .OF_EX(OF_EX_instr),
    .for_op2_mux(forwarding_unit_1_for_op2_mux), .for_op1_op2_mux(forwarding_unit_1_for_op1_op2_mux),
    .out_7(forwarding_unit_1_out_7), .for_op2_mux_2(forwarding_unit_1_for_op2_mux_2),
    .for_op1_A__mux(forwarding_unit_1_for_op1_a__mux), .for_op2_B__mux(forwarding_unit_1_for_op2_b__mux));
  not not_1 (Stall, data_lock_unit_1_out_3);
  Register #(.width(32), .trigger("falling")) PC (
    .D(multiplexer_1_out), .en(Stall), .Q(PC_q), .clk(Clock), .clr(Reset));
  assign bit_extender_1_out = {{5{IF_OF_instr[26]}}, IF_OF_instr[26:0]};  // Bit_Extender bit_extender_1
  Multiplexer #(.width(32), .enable("false")) multiplexer_1 (
    .in0(adder_1_out), .in1(branchTarget), .out(multiplexer_1_out), .sel(isBranchTaken));
  Shifter #(.width(32)) shifter_1 (.in(bit_extender_1_out), .\dist (5'b00010), .out(shifter_1_out));
  Register #(.width(32), .trigger("falling")) register_1 (
    .D(register_3_q), .Q(register_1_q), .clk(Clock), .clr(Reset));  // open: en
  ALU alu_1 (
    .A(multiplexer_6_out), .B(multiplexer_4_out), .ALUsignals(control_1_alusignals_2),
    .aluResult(alu_1_aluresult), .is_2(alu_1_is_2), .is(alu_1_is));
  Register #(.width(32), .trigger("falling")) register_2 (
    .D(register_1_q), .Q(register_2_q), .clk(Clock), .clr(Reset));  // open: en
  Adder #(.width(32)) adder_1 (.a(32'h4), .b(PC_q), .out(adder_1_out));  // open: cin, cout
  Register #(.width(32), .trigger("falling")) register_3 (
    .D(PC_q), .en(Stall), .Q(register_3_q), .clk(Clock), .clr(Reset));
  Calculate_Immediate calculate_immediate_1 (.imm(IF_OF_instr[17:0]), .immx(calculate_immediate_1_immx));
  Adder #(.width(32)) adder_2 (.a(shifter_1_out), .b(register_3_q), .out(adder_2_out));  // open: cin, cout
  Register #(.width(32), .trigger("falling")) register_4 (
    .D(adder_2_out), .Q(register_4_q), .clk(Clock), .clr(Reset));  // open: en
  Multiplexer #(.width(32), .enable("false")) multiplexer_2 (
    .in0(register_4_q), .in1(multiplexer_6_out), .out(branchTarget), .sel(control_1_isret_2));
  Register #(.width(32), .trigger("falling")) register_5 (
    .D(register_2_q), .Q(register_5_q), .clk(Clock), .clr(Reset));  // open: en
  Multiplexer #(.width(32), .enable("false")) multiplexer_3 (
    .in0(multiplexer_9_out), .in1(calculate_immediate_1_immx), .out(multiplexer_3_out),
    .sel(control_unit_1_isimmediate));
  Register #(.width(32), .trigger("falling")) register_6 (
    .D(multiplexer_3_out), .Q(register_6_q), .clk(Clock), .clr(Reset));  // open: en
  Multiplexer #(.select(2), .width(32), .enable("false")) multiplexer_4 (
    .in0(register_6_q), .in1(data), .in2(aluResult), .in3(aluResult), .out(multiplexer_4_out),
    .sel(forwarding_unit_1_for_op2_b__mux));
  Register #(.width(32), .trigger("falling")) register_7 (
    .D(alu_1_aluresult), .Q(aluResult), .clk(Clock), .clr(Reset));  // open: en
  Multiplexer #(.width(32), .enable("false")) multiplexer_5 (
    .in0(register_9_q), .in1(data), .out(multiplexer_5_out), .sel(forwarding_unit_1_for_op2_mux));
  Register #(.width(32), .trigger("falling")) register_8 (
    .D(multiplexer_12_out), .Q(register_8_q), .clk(Clock), .clr(Reset));  // open: en
  Multiplexer #(.select(2), .width(32), .enable("false")) multiplexer_6 (
    .in0(register_8_q), .in1(data), .in2(aluResult), .in3(aluResult), .out(multiplexer_6_out),
    .sel(forwarding_unit_1_for_op1_a__mux));
  Flags flags_1 (
    .isCmp(control_1_alusignals_2[0]), .is(alu_1_is), .is_2(alu_1_is_2), .flags_GT(flags_1_flags_gt),
    .flags_E(flags_1_flags_e));
  Register #(.width(32), .trigger("falling")) register_9 (
    .D(multiplexer_10_out), .Q(register_9_q), .clk(Clock), .clr(Reset));  // open: en
  Memory_Unit memory_unit_1 (
    .MAR(aluResult), .ldResult(memory_unit_1_ldresult), .MDR(multiplexer_5_out),
    .isSt(control_ex_ma_1_isst_2), .isLd(control_ex_ma_1_isld_2), .Clock(Clock), .Reset(Reset));
  Register #(.width(32), .trigger("falling")) register_10 (
    .D(memory_unit_1_ldresult), .Q(register_10_q), .clk(Clock), .clr(Reset));  // open: en
  Adder #(.width(32)) adder_3 (.a(register_5_q), .b(32'h4), .out(adder_3_out));  // open: cin, cout
  Clock u_Clock (.out(Clock));
  ROM #(.addrWidth(24), .dataWidth(32)) rom_1 (.addr(PC_q[25:2]), .data(rom_1_data));  // open: sel
  Multiplexer #(.width(4), .enable("false")) multiplexer_7 (
    .in0(IF_OF_instr[21:18]), .in1(4'b1111), .out(multiplexer_7_out), .sel(control_unit_1_isret));
  Multiplexer #(.width(4), .enable("false")) multiplexer_8 (
    .in0(IF_OF_instr[17:14]), .in1(IF_OF_instr[25:22]), .out(multiplexer_8_out), .sel(control_unit_1_isst));
  Multiplexer #(.width(32), .enable("false")) multiplexer_9 (
    .in0(register_file_1_readd2), .in1(data), .out(multiplexer_9_out), .sel(forwarding_unit_1_for_op1_op2_mux));
  Register #(.width(32), .trigger("falling")) register_11 (
    .D(multiplexer_9_out), .Q(register_11_q), .clk(Clock), .clr(Reset));  // open: en
  Multiplexer #(.width(32), .enable("false")) multiplexer_10 (
    .in0(register_11_q), .in1(data), .out(multiplexer_10_out), .sel(forwarding_unit_1_for_op2_mux_2));
  Register #(.width(32), .trigger("falling")) register_12 (
    .D(OF_EX_instr), .Q(EX_MA_instr), .clk(Clock), .clr(Reset));  // open: en
  Register #(.width(32), .trigger("falling")) register_13 (
    .D(aluResult), .Q(register_13_q), .clk(Clock), .clr(Reset));  // open: en
  Multiplexer #(.select(2), .width(32), .enable("false")) multiplexer_11 (
    .in0(register_13_q), .in1(register_10_q), .in2(adder_3_out), .out(data), .sel(control_ma_rw_1_isld_2));  // open: in3
  Hex_Digit_Display hex_digit_display_1 (.value(register_file_1_displayd_7));  // open: dp
  Hex_Digit_Display hex_digit_display_2 (.value(register_file_1_displayd_3[31:28]));  // open: dp
  Register_File register_file_1 (
    .ReadA1(multiplexer_7_out), .ReadA2(multiplexer_8_out), .WriteE(isWb), .WriteD(data),
    .ReadD1(register_file_1_readd1), .ReadD2(register_file_1_readd2), .Clock(Clock), .Reset(Reset),
    .DisplayD({register_file_1_displayd_3[31:28], register_file_1_displayd_7, register_file_1_displayd_6, register_file_1_displayd_5, register_file_1_displayd_4, register_file_1_displayd_3[11:8], register_file_1_displayd_2, register_file_1_displayd}),
    .DisplayA(Display_Address), .WriteA(address));
  Multiplexer #(.width(32), .enable("false")) multiplexer_12 (
    .in0(register_file_1_readd1), .in1(data), .out(multiplexer_12_out), .sel(forwarding_unit_1_out_7));
  Multiplexer #(.width(32), .enable("false")) multiplexer_13 (
    .in0(IF_OF_instr), .in1(32'h68000000), .out(multiplexer_13_out), .sel(Bubble));
  Register #(.width(32), .trigger("falling")) register_14 (
    .D(multiplexer_13_out), .Q(OF_EX_instr), .clk(Clock), .clr(Reset));  // open: en
  control control_1 (
    .Bubble(Bubble), .isRet(control_unit_1_isret), .isWb(control_unit_1_iswb),
    .ALUsignals(control_unit_1_alusignals), .isLd(control_unit_1_isld), .isSt(control_unit_1_isst),
    .isCall(control_unit_1_iscall), .isBeq(control_unit_1_isbeq), .isBgt(control_unit_1_isbgt),
    .isUBranch(control_unit_1_isubranch), .isRet_2(control_1_isret_2), .isWb_2(control_1_iswb_2),
    .ALUsignals_2(control_1_alusignals_2), .isLd_2(control_1_isld_2), .isSt_2(control_1_isst_2),
    .isCall_2(control_1_iscall_2), .isBeq_2(control_1_isbeq_2), .isBgt_2(control_1_isbgt_2),
    .isUBranch_2(control_1_isubranch_2), .in_11(Clock), .in_12(Reset));
  Register #(.width(32), .trigger("falling")) register_15 (
    .D(EX_MA_instr), .Q(MA_RW_instr), .clk(Clock), .clr(Reset));  // open: en
  Hex_Digit_Display hex_digit_display_3 (.value(register_file_1_displayd_6));  // open: dp
  Branch_Unit branch_unit_1 (
    .isBeq(control_1_isbeq_2), .isUBranch(control_1_isubranch_2), .flags_E(flags_1_flags_e),
    .isBgt(control_1_isbgt_2), .flags_GT(flags_1_flags_gt), .isBranchTaken(isBranchTaken));
  control_ex_ma control_ex_ma_1 (
    .isLd(control_1_isld_2), .isSt(control_1_isst_2), .isCall(control_1_iscall_2), .isWb(control_1_iswb_2),
    .in_6(Reset), .in_5(Clock), .isLd_2(control_ex_ma_1_isld_2), .isSt_2(control_ex_ma_1_isst_2),
    .isCall_2(control_ex_ma_1_iscall_2), .isWb_2(control_ex_ma_1_iswb_2));
  Multiplexer #(.width(4), .enable("false")) multiplexer_14 (
    .in0(MA_RW_instr[25:22]), .in1(4'b1111), .out(address), .sel(control_ma_rw_1_isld_2[1]));
  Hex_Digit_Display hex_digit_display_4 (.value(register_file_1_displayd_5));  // open: dp
  Register #(.width(32), .trigger("falling")) register_16 (
    .D(multiplexer_15_out), .en(Stall), .Q(IF_OF_instr), .clk(Clock), .clr(Reset));
  Control_Unit control_unit_1 (
    .isSt(control_unit_1_isst), .isLd(control_unit_1_isld), .isBeq(control_unit_1_isbeq),
    .isBgt(control_unit_1_isbgt), .isRet(control_unit_1_isret), .I_bit(IF_OF_instr[26]),
    .isImmediate(control_unit_1_isimmediate), .opcode(IF_OF_instr[31:27]), .isWb(control_unit_1_iswb),
    .isUbranch(control_unit_1_isubranch), .isCall(control_unit_1_iscall),
    .ALUsignals(control_unit_1_alusignals));
  control_ma_rw control_ma_rw_1 (
    .isLd(control_ex_ma_1_isld_2), .isCall(control_ex_ma_1_iscall_2), .isWb(control_ex_ma_1_iswb_2),
    .in_5(Reset), .in_4(Clock), .isLd_2(control_ma_rw_1_isld_2[0]), .isCall_2(control_ma_rw_1_isld_2[1]),
    .isWb_2(isWb));
  Hex_Digit_Display hex_digit_display_5 (.value(register_file_1_displayd_3[11:8]));  // open: dp
  Hex_Digit_Display hex_digit_display_6 (.value(register_file_1_displayd_4));  // open: dp
  Multiplexer #(.width(32), .enable("false")) multiplexer_15 (
    .in0(rom_1_data), .in1(32'h68000000), .out(multiplexer_15_out), .sel(isBranchTaken));
  Hex_Digit_Display hex_digit_display_7 (.value(register_file_1_displayd_2));  // open: dp
  Hex_Digit_Display hex_digit_display_8 (.value(register_file_1_displayd));  // open: dp
  or or_1 (Bubble, ~Stall, isBranchTaken);  // OR_Gate

  // Notes on the sheet:
  //   from RW to MA for op2
  //   from RW/MA for A
  //   from RW to EX for op2
  //   from RW/MA for B
  //   from RW, MA
  //   pc
  //   from RW to OF for op2
  //   from RW to OF for op1
  //   PC
  //   ALUsignals
  //   PC
  //   pc+4
  //   PC
  //   imm
  //   offset
  //   branchTarget
  //   bT
  //   B
  //   ALU
  //   PC
  //   calc immx
  //   immx
  //   B
  //   A
  //   aluResult
  //   MAR
  //   Memory
  //   Unit
  //   ldResult
  //   pc
  //   Instruction Memory
  //   instruction
  //   rs2
  //   isImmediate
  //   A
  //   is>
  //   Flags
  //   isCmp
  //   from RW
  //   op2
  //   from RW
  //   MDR
  //   isLd
  //   ldRes
  //   instruction
  //   contents of rom_1 (hex, n*v repeats v):
  //   4c00000a 98000002 90000000 2c000001 88000003 4c400001 a0000000 fb80008 7c380000 7ff80004 c000001
  //   9ffffff8 77f80004 74380000 7b80008 10404000 a0000000
  //   instr from IF-OF
  //   rs1
  //   rd
  //   isSt
  //   Register
  //   File
  //   op1
  //   op2
  //   op2
  //   flags(GT)
  //   flags(E)
  //   inst
  //   isSt
  //   aluRes
  //   data
  //   isRet
  //   isWb
  //   E
  //   address
  //   A
  //   data
  //   D
  //   from RW
  //   inst
  //   Branch
  //   Unit
  //   inst
  //   isLd
  //   isCall
  //   nop
  //   isBeq
  //   isBgt
  //   isUBranch
  //   opcode
  //   I bit
  //   instruction
  //   CONTROL
  //   UNIT
  //   instr from OF-EX
endmodule

module control_ma_rw (
  input  isLd,
  input  isCall,
  input  isWb,
  input  in_4,
  input  in_5,
  output isLd_2,
  output isCall_2,
  output isWb_2
);

  Register #(.width(1), .trigger("falling")) register_1 (.D(isLd), .Q(isLd_2), .clk(in_4), .clr(in_5));  // open: en
  Register #(.width(1), .trigger("falling")) register_2 (.D(isCall), .Q(isCall_2), .clk(in_4), .clr(in_5));  // open: en
  Register #(.width(1), .trigger("falling")) register_3 (.D(isWb), .Q(isWb_2), .clk(in_4), .clr(in_5));  // open: en
endmodule

module control_ex_ma (
  input  isLd,
  input  isSt,
  input  isCall,
  input  isWb,
  input  in_5,
  input  in_6,
  output isLd_2,
  output isSt_2,
  output isCall_2,
  output isWb_2
);

  Register #(.width(1), .trigger("falling")) register_1 (.D(isLd), .Q(isLd_2), .clk(in_5), .clr(in_6));  // open: en
  Register #(.width(1), .trigger("falling")) register_2 (.D(isSt), .Q(isSt_2), .clk(in_5), .clr(in_6));  // open: en
  Register #(.width(1), .trigger("falling")) register_3 (.D(isCall), .Q(isCall_2), .clk(in_5), .clr(in_6));  // open: en
  Register #(.width(1), .trigger("falling")) register_4 (.D(isWb), .Q(isWb_2), .clk(in_5), .clr(in_6));  // open: en
endmodule

module check_A_opcode_reader (
  input  [4:0] opcode,
  output out_2
);

  wire b_beq_bgt_call_out, mov_not_out, nop_out, or_1_out;

  and b_beq_bgt_call (b_beq_bgt_call_out, opcode[4], ~opcode[3], ~opcode[2]);  // AND_Gate
  or or_1 (or_1_out, b_beq_bgt_call_out, nop_out, mov_not_out);
  and nop (nop_out, ~opcode[4], opcode[3], opcode[2], ~opcode[1], opcode[0]);  // AND_Gate
  not not_1 (out_2, or_1_out);
  and mov_not (mov_not_out, ~opcode[4], opcode[3], ~opcode[2], ~opcode[1]);  // AND_Gate

  // Notes on the sheet:
  //   reduced to 100xx
  //   if any one true, no conflict
  //   return false when no conflict, else there can be a conflict
  //   0100x
endmodule

module check_B_opcode_writer (
  input  [4:0] in_1,
  output out_2
);

  wire _100x0_out, _1000x_out, cmp_out, nop_out, ret_out, st_out;

  and nop (nop_out, ~in_1[4], in_1[3], in_1[2], ~in_1[1], in_1[0]);  // AND_Gate
  and cmp (cmp_out, ~in_1[4], ~in_1[3], in_1[2], ~in_1[1], in_1[0]);  // AND_Gate
  and st (st_out, ~in_1[4], in_1[3], in_1[2], in_1[1], in_1[0]);  // AND_Gate
  and _1000x (_1000x_out, in_1[4], ~in_1[3], ~in_1[2], ~in_1[1]);  // AND_Gate
  nor nor_1 (out_2, nop_out, cmp_out, st_out, _1000x_out, _100x0_out, ret_out);
  and _100x0 (_100x0_out, in_1[4], ~in_1[3], ~in_1[2], ~in_1[0]);  // AND_Gate
  and ret (ret_out, in_1[4], ~in_1[3], in_1[2], ~in_1[1], ~in_1[0]);  // AND_Gate

  // Notes on the sheet:
  //   return false
  //   b,beq,bgt
endmodule

module select_rs1_rs2_and_rd (
  input  [31:0] A,
  input  [31:0] B,
  output out_3,
  output [3:0] rd,
  output [3:0] rs2,
  output [3:0] rs1_ra
);

  wire call_out, not_1_out, ret_out, st_out;

  and ret (ret_out, A[31], ~A[30], A[29], ~A[28], ~A[27]);  // AND_Gate
  Multiplexer #(.width(4), .enable("false")) multiplexer_1 (.in0(A[21:18]), .in1(4'b1111), .out(rs1_ra), .sel(ret_out));
  and st (st_out, ~A[31], A[30], A[29], A[28], A[27]);  // AND_Gate
  Multiplexer #(.width(4), .enable("false")) multiplexer_2 (.in0(A[17:14]), .in1(A[25:22]), .out(rs2), .sel(st_out));
  not not_1 (not_1_out, A[26]);
  Multiplexer #(.enable("false")) multiplexer_3 (.in0(not_1_out), .in1(1'b1), .out(out_3), .sel(st_out));
  and call (call_out, B[31], ~B[30], ~B[29], B[28], B[27]);  // AND_Gate
  Multiplexer #(.width(4), .enable("false")) multiplexer_4 (.in0(B[25:22]), .in1(4'b1111), .out(rd), .sel(call_out));

  // Notes on the sheet:
  //   forwarding from B->A
  //   rs1
  //   ra
  //   rs2
  //   rs2(imm or reg)
  //   A.rd
endmodule

module Conflict_detection_forwarding (
  input  [31:0] A,
  input  [31:0] B,
  output out_3,
  output out_4
);

  wire and_1_out, and_3_out, and_5_out, check_a_opcode_reader_1_out_2, check_a_opcode_source2_1_out_2,
       check_b_opcode_writer_1_out_2, comparator_1_eq, comparator_2_eq, select_rs1_rs2_and_rd_1_out_3;
  wire [3:0] select_rs1_rs2_and_rd_1_rd, select_rs1_rs2_and_rd_1_rs1_ra, select_rs1_rs2_and_rd_1_rs2;

  check_A_opcode_reader check_a_opcode_reader_1 (.opcode(A[31:27]), .out_2(check_a_opcode_reader_1_out_2));
  and and_1 (and_1_out, check_a_opcode_reader_1_out_2, check_b_opcode_writer_1_out_2);
  check_B_opcode_writer check_b_opcode_writer_1 (.in_1(B[31:27]), .out_2(check_b_opcode_writer_1_out_2));
  check_A_opcode_source2 check_a_opcode_source2_1 (.opcode(A[31:27]), .out_2(check_a_opcode_source2_1_out_2));
  and and_2 (out_3, and_1_out, comparator_1_eq);
  and and_3 (and_3_out, check_a_opcode_source2_1_out_2, check_b_opcode_writer_1_out_2);
  select_rs1_rs2_and_rd select_rs1_rs2_and_rd_1 (
    .A(A), .B(B), .rs1_ra(select_rs1_rs2_and_rd_1_rs1_ra), .rs2(select_rs1_rs2_and_rd_1_rs2),
    .rd(select_rs1_rs2_and_rd_1_rd), .out_3(select_rs1_rs2_and_rd_1_out_3));
  Comparator #(.width(4)) comparator_1 (
    .a(select_rs1_rs2_and_rd_1_rs1_ra), .b(select_rs1_rs2_and_rd_1_rd), .eq(comparator_1_eq));  // open: gt, lt
  Comparator #(.width(4)) comparator_2 (
    .a(select_rs1_rs2_and_rd_1_rs2), .b(select_rs1_rs2_and_rd_1_rd), .eq(comparator_2_eq));  // open: gt, lt
  and and_4 (out_4, and_3_out, and_5_out);
  and and_5 (and_5_out, comparator_2_eq, select_rs1_rs2_and_rd_1_out_3);

  // Notes on the sheet:
  //   operand 1 conflict
  //   operand 2 conflict
endmodule

module check_A_opcode_source2 (
  input  [4:0] opcode,
  output out_2
);

  wire b_beq_bgt_call_out, nop_out, or_1_out;

  and b_beq_bgt_call (b_beq_bgt_call_out, opcode[4], ~opcode[3], ~opcode[2]);  // AND_Gate
  or or_1 (or_1_out, b_beq_bgt_call_out, nop_out);
  and nop (nop_out, ~opcode[4], opcode[3], opcode[2], ~opcode[1], opcode[0]);  // AND_Gate
  not not_1 (out_2, or_1_out);

  // Notes on the sheet:
  //   reduced to 100xx
endmodule

module Data_Lock_Unit (
  input  [31:0] A,
  input  [31:0] B,
  output out_3
);

  wire conflict_detection_forwarding_1_out_3, conflict_detection_forwarding_1_out_4, load_out, or_1_out;

  Conflict_detection_forwarding conflict_detection_forwarding_1 (
    .B(A), .A(B), .out_3(conflict_detection_forwarding_1_out_3), .out_4(conflict_detection_forwarding_1_out_4));
  or or_1 (or_1_out, conflict_detection_forwarding_1_out_3, conflict_detection_forwarding_1_out_4);
  and load (load_out, ~B[31], B[30], B[29], B[28], ~B[27]);  // AND_Gate
  and and_1 (out_3, load_out, or_1_out);

  // Notes on the sheet:
  //   IF-OF
  //   OF-EX
  //   load-use
endmodule

module Forwarding_Unit (
  input  [31:0] MA_RW,
  input  [31:0] EX_MA,
  input  [31:0] IF_OF,
  input  [31:0] OF_EX,
  output for_op2_mux,
  output for_op1_op2_mux,
  output out_7,
  output for_op2_mux_2,
  output [1:0] for_op1_A__mux,
  output [1:0] for_op2_B__mux
);

  wire conflict_detection_forwarding_4_out_4, store_out;

  Conflict_detection_forwarding conflict_detection_forwarding_1 (
    .B(MA_RW), .A(EX_MA), .out_4(for_op2_mux));  // open: out_3
  Conflict_detection_forwarding conflict_detection_forwarding_2 (
    .B(MA_RW), .A(IF_OF), .out_3(out_7), .out_4(for_op1_op2_mux));
  Conflict_detection_forwarding conflict_detection_forwarding_3 (
    .B(MA_RW), .A(OF_EX), .out_3(for_op1_A__mux[0]), .out_4(for_op2_mux_2));
  Conflict_detection_forwarding conflict_detection_forwarding_4 (
    .B(EX_MA), .A(OF_EX), .out_3(for_op1_A__mux[1]), .out_4(conflict_detection_forwarding_4_out_4));
  and store (store_out, OF_EX[27], OF_EX[28], OF_EX[29], OF_EX[30], ~OF_EX[31]);  // AND_Gate
  Multiplexer #(.enable("false")) multiplexer_1 (
    .in0(for_op2_mux_2), .in1(1'b0), .out(for_op2_B__mux[0]), .sel(store_out));
  Multiplexer #(.enable("false")) multiplexer_2 (
    .in0(conflict_detection_forwarding_4_out_4), .in1(1'b0), .out(for_op2_B__mux[1]), .sel(store_out));

  // Notes on the sheet:
  //   if instr in OF-EX is a store, we want RW-MA forwd. wherever possible
  //   RW->MA
  //   RW->OF
  //   RW->EX
  //   MA->EX
  //   00 - A or B, 01 - data, 10- aluresult, 11-aluresult(MA->EX chosen)
  //   RW->EX or MA->EX
endmodule
